# Fritzing sketch diagrama semaforos (saved by Fritzing 0.9.3b)
breadboards: 1

parts:
  R1 = Rotary Potentiometer (Large) [maximum_resistance=100kΩ package=THT]
  S1 = Pushbutton [package="[THT]"]
  R2 = Resistor [tolerance=±5% resistance=220 package="0805 [SMD]"]
  R3 = Resistor [tolerance=±5% resistance=220 package="0805 [SMD]"]
  R4 = Resistor [tolerance=±5% resistance=220 package="0805 [SMD]"]
  R5 = Resistor [tolerance=±5% resistance=220 package="0805 [SMD]"]
  R6 = Resistor [tolerance=±5% resistance=220 package="0805 [SMD]"]
  LED1 = LED - 5mm [color="Red (633nm)" package="5 mm [THT]"]
  LED2 = LED - 5mm [color="Yellow (595nm)" package="5 mm [THT]"]
  LED3 = LED - 5mm [color="Green (570nm)" package="5 mm [THT]"]
  LED4 = LED - 5mm [color="Green (570nm)" package="5 mm [THT]"]
  LED5 = LED - 5mm [color="Red (633nm)" package="5 mm [THT]"]
  Componente1 = Arduino Uno (Rev3)

nets:
  N1: R1.leg1, S1.Pin_1, S1.Pin_2, LED2.cathode, LED3.cathode, LED4.cathode, LED5.cathode, Componente1.GND
  N2: R1.wiper, Componente1.A5/SCL
  N3: R1.leg2, S1.Pin_3, S1.Pin_4, LED1.cathode, Componente1.D8, Componente1.5V
  N4: R2.Pin_0, LED3.anode, Componente1.D11_PWM/MOSI
  N5: R3.Pin_0, LED2.anode, Componente1.D10_PWM/SS
  N6: R4.Pin_0, LED1.anode, Componente1.D9_PWM
  N7: R5.Pin_1, LED5.anode, Componente1.D13/SCK
  N8: R6.Pin_0, LED4.anode, Componente1.D12/MISO
